// Logisim project relogio-digital.circ as structural Verilog
module cont_01 (
  input  clk,
  input  reset,
  output [3:0] display,
  output prox
);

  wire and_1_out;
  wire [3:0] adder_1_out;

  Register #(.width(4)) register_1 (.D(adder_1_out), .clk(clk), .Q(display), .clr(prox));  // open: en
  Hex_Digit_Display hex_digit_display_1 (.value(display));  // open: dp
  or or_1 (prox, and_1_out, reset);
  and and_1 (and_1_out, ~display[0], display[1], ~display[2], display[3]);  // AND_Gate
  Adder #(.width(4)) adder_1 (.a(display), .b(4'b0001), .out(adder_1_out));  // open: cin, cout
endmodule

module cont_02 (
  input  reset,
  input  clk,
  output [3:0] dezena,
  output [3:0] unidade,
  output prox
);

  wire cont_01_2_prox, or_1_out;

  and and_1 (prox, ~dezena[0], dezena[1], dezena[2], ~dezena[3]);  // AND_Gate
  or or_1 (or_1_out, prox, reset);
  Hex_Digit_Display hex_digit_display_1 (.value(dezena));  // open: dp
  cont_01 cont_01_1 (.display(dezena), .clk(cont_01_2_prox), .reset(or_1_out));  // open: prox
  Hex_Digit_Display hex_digit_display_2 (.value(unidade));  // open: dp
  cont_01 cont_01_2 (.display(unidade), .clk(clk), .reset(or_1_out), .prox(cont_01_2_prox));
endmodule

module cont_03 (
  input  reset,
  input  clk,
  output [3:0] dezena,
  output [3:0] unidade,
  output prox
);

  wire cont_01_2_prox, or_1_out;

  nor nor_1 (prox, dezena[3], dezena[2], ~dezena[1], dezena[0], unidade[3], ~unidade[2], unidade[1], unidade[0]);  // NOR_Gate
  or or_1 (or_1_out, prox, reset);
  Hex_Digit_Display hex_digit_display_1 (.value(dezena));  // open: dp
  cont_01 cont_01_1 (.display(dezena), .clk(cont_01_2_prox), .reset(or_1_out));  // open: prox
  Hex_Digit_Display hex_digit_display_2 (.value(unidade));  // open: dp
  cont_01 cont_01_2 (.display(unidade), .clk(clk), .reset(or_1_out), .prox(cont_01_2_prox));
endmodule

module cont_full (
  input  clk,
  input  resetn,
  input  altH,
  input  altM,
  input  altS,
  output [3:0] DHR,
  output [3:0] UHR,
  output [3:0] DMR,
  output [3:0] UMR,
  output [3:0] DSR,
  output [3:0] USR
);

  wire cont_02_1_prox, cont_02_2_prox, or_1_out, or_2_out, or_3_out;

  cont_03 cont_03_1 (.dezena(DHR), .reset(resetn), .clk(or_1_out), .unidade(UHR));  // open: prox
  or or_1 (or_1_out, altH, cont_02_1_prox);
  cont_02 cont_02_1 (.dezena(DMR), .prox(cont_02_1_prox), .reset(resetn), .clk(or_2_out), .unidade(UMR));
  or or_2 (or_2_out, altM, cont_02_2_prox);
  cont_02 cont_02_2 (.dezena(DSR), .prox(cont_02_2_prox), .reset(resetn), .clk(or_3_out), .unidade(USR));
  or or_3 (or_3_out, clk, altS);
endmodule

module circuito_externo (
  input  in_1,
  input  in_2
);

  wire A, ALARM, ALARM1, ALTER, ALTER1, ALTER2, altH, altM, altS, C, CLK_RELOGIO_out, CLOCK, comparator_1_eq,
       comparator_2_eq, comparator_3_eq, comparator_4_eq, comparator_5_eq, comparator_6_eq, counter_3_carry,
       H, Ha, M, Ma, MODE, N, NULL, or_1_out, or_2_out, PAUSE, RESET, S, Sa, SELECT;
  wire [1:0] counter_1_q, counter_2_q;
  wire [3:0] DH, DHR, DHX, DM, DMR, DMX, DS, DSR, DSX, UH, UHR, UHX, UM, UMR, UMX, US, USR, USX;

  Counter #(.width(2), .max('h3)) counter_1 (
    .up(1'b1), .clk(SELECT), .Q(counter_1_q));  // open: clr, load, count, D, carry
  Counter #(.width(2), .max('h2)) counter_2 (
    .up(1'b1), .clk(MODE), .Q(counter_2_q));  // open: clr, load, count, D, carry
  Counter #(.width(2), .max('h1)) counter_3 (
    .up(1'b1), .clk(PAUSE), .carry(counter_3_carry));  // open: clr, load, count, D, Q
  Demultiplexer #(.select(2), .enable("false")) demultiplexer_1 (
    .out0(Sa), .out1(Ma), .out2(Ha), .in(ALTER1), .sel(counter_1_q));  // open: out3
  Demultiplexer #(.select(2), .enable("false")) demultiplexer_2 (
    .out1(ALTER1), .out2(ALTER2), .in(ALTER), .sel(counter_2_q));  // open: out0, out3
  and and_1 (ALARM, ALARM1, counter_3_carry);
  Clock CLK_RELOGIO (.out(CLK_RELOGIO_out));
  and and_2 (CLOCK, CLK_RELOGIO_out, counter_3_carry);
  Demultiplexer #(.select(2), .enable("false")) demultiplexer_3 (
    .out0(altS), .out1(altM), .out2(altH), .in(ALTER2), .sel(counter_1_q));  // open: out3
  and and_3 (S, ~counter_1_q[0], ~counter_1_q[1]);  // AND_Gate
  and and_4 (N, ~counter_2_q[0], ~counter_2_q[1]);  // AND_Gate
  and and_5 (H, ~counter_1_q[0], counter_1_q[1]);  // AND_Gate
  and and_6 (M, counter_1_q[0], ~counter_1_q[1]);  // AND_Gate
  and and_7 (C, ~counter_2_q[0], counter_2_q[1]);  // AND_Gate
  and and_8 (A, counter_2_q[0], ~counter_2_q[1]);  // AND_Gate
  and and_9 (NULL, counter_1_q[0], counter_1_q[1]);
  Multiplexer #(.width(4), .enable("false")) multiplexer_1 (.in0(DM), .in1(DMX), .out(DMR), .sel(A));
  Multiplexer #(.width(4), .enable("false")) multiplexer_2 (.in0(DS), .in1(DSX), .out(DSR), .sel(A));
  Multiplexer #(.width(4), .enable("false")) multiplexer_3 (.in0(DH), .in1(DHX), .out(DHR), .sel(A));
  Register #(.width(1)) register_1 (.D(ALARM1), .clr(ALARM));  // open: en, clk, Q
  Button button_1 (.out(SELECT));
  Button button_2 (.out(RESET));
  Button button_3 (.out(PAUSE));
  Hex_Digit_Display hex_digit_display_1 (.value(DHR));  // open: dp
  Multiplexer #(.width(4), .enable("false")) multiplexer_4 (.in0(UM), .in1(UMX), .out(UMR), .sel(A));
  Multiplexer #(.width(4), .enable("false")) multiplexer_5 (.in0(US), .in1(USX), .out(USR), .sel(A));
  Multiplexer #(.width(4), .enable("false")) multiplexer_6 (.in0(UH), .in1(UHX), .out(UHR), .sel(A));
  LED led_1 (.in(H));
  Hex_Digit_Display hex_digit_display_2 (.value(UHR));  // open: dp
  LED led_2 (.in(C));
  LED led_3 (.in(NULL));
  LED led_4 (.in(M));
  Hex_Digit_Display hex_digit_display_3 (.value(UMR));  // open: dp
  Hex_Digit_Display hex_digit_display_4 (.value(DMR));  // open: dp
  LED led_5 (.in(A));
  LED led_6 (.in(ALARM));
  or or_1 (or_1_out, RESET, in_1);
  Hex_Digit_Display hex_digit_display_5 (.value(DSR));  // open: dp
  cont_full cont_full_1 (
    .clk(CLOCK), .UHR(UH), .DMR(DM), .UMR(UM), .DSR(DS), .USR(US), .resetn(or_1_out), .altH(altH),
    .altM(altM), .altS(altS), .DHR(DH));
  LED led_7 (.in(S));
  Hex_Digit_Display hex_digit_display_6 (.value(USR));  // open: dp
  LED led_8 (.in(N));
  or or_2 (or_2_out, RESET, in_2);
  Button button_4 (.out(MODE));
  Button button_5 (.out(ALTER));
  cont_full cont_full_2 (
    .clk(1'b0), .UHR(UHX), .DMR(DMX), .UMR(UMX), .DSR(DSX), .USR(USX), .resetn(or_2_out), .altH(Ha),
    .altM(Ma), .altS(Sa), .DHR(DHX));
  Comparator #(.width(4)) comparator_1 (.a(DH), .b(DHX), .eq(comparator_1_eq));  // open: gt, lt
  Comparator #(.width(4)) comparator_2 (.a(UH), .b(UHX), .eq(comparator_2_eq));  // open: gt, lt
  Comparator #(.width(4)) comparator_3 (.a(DM), .b(DMX), .eq(comparator_3_eq));  // open: gt, lt
  Comparator #(.width(4)) comparator_4 (.a(UM), .b(UMX), .eq(comparator_4_eq));  // open: gt, lt
  Comparator #(.width(4)) comparator_5 (.a(DS), .b(DSX), .eq(comparator_5_eq));  // open: gt, lt
  Comparator #(.width(4)) comparator_6 (.a(US), .b(USX), .eq(comparator_6_eq));  // open: gt, lt
  and and_10 (ALARM1, comparator_1_eq, comparator_2_eq, comparator_3_eq, comparator_4_eq, comparator_5_eq, comparator_6_eq);

  // Other names for the same wires on the sheet: s_t = A

  // Notes on the sheet:
  //   CIRCUITO 003
  //   CIRCUITO 002
  //   CIRCUITO PRINCIPAL - RELOGIO 
  //   CIRCUTO 001
  //   CIRCUITO 003
endmodule
